# Fritzing sketch Placa (saved by Fritzing 0.9.3b)

parts:
  U1 = ESP32-WROOM-32D-NodeMCU
  M1 = Getriebemotor
  M2 = Getriebemotor
  L298N1 = L298N DC motor driver
  HC-SR04_Sensor_1 = HC-SR04 Ultrasonic Distance Sensor
  HC-SR04_Sensor_2 = HC-SR04 Ultrasonic Distance Sensor
  ESP32_-_Front1 = ESP32 - CAM
  J1 = Basic Servo
  KY-1 = Keyes Photo Resistor Sensor [package=THT]
  Componente1 = KY-033 Tracing Black White Line Hunting Sensor Module For Arduino
  Componente3 = KY-033 Tracing Black White Line Hunting Sensor Module For Arduino
  Componente4 = Passive Buzzer
  U2 = LIPO-1000mAh [package=lipo-1000]
  U3 = LIPO-1000mAh [package=lipo-1000]
  U4 = LIPO-1000mAh [package=lipo-1000]
  U5 = LIPO-1000mAh [package=lipo-1000]

nets:
  3.3V: U1.3.3V, J1.vcc, KY-1.power
  GND: U1.G32, U1.GND#13, L298N1.GND, HC-SR04_Sensor_1.GND, HC-SR04_Sensor_2.GND, ESP32_-_Front1.GND#7, KY-1.signal, KY-1.ground, Componente1.GND, Componente3.GND, U2.-, U4.-
  N1: U1.G33, Componente3.S
  N2: U1.G25, Componente1.S
  N3: U1.G26, L298N1.IN1
  N4: U1.G27, L298N1.IN2
  N5: U1.G14, L298N1.IN3
  N6: U1.G12, L298N1.IN4
  5V: U1.5V, L298N1.5V, HC-SR04_Sensor_1.VCC
  N7: U1.G15, L298N1.ENB
  N8: U1.G2, L298N1.ENA
  N9: U1.G4, J1.pulse
  N10: U1.G16, HC-SR04_Sensor_2.ECHO
  N11: U1.G17, HC-SR04_Sensor_2.TRIG
  N12: U1.G5, HC-SR04_Sensor_1.TRIG
  N13: U1.G18, HC-SR04_Sensor_1.ECHO
  N14: U1.GND#44, J1.gnd
  N15: U1.RXD, ESP32_-_Front1.GPIO1_/_TX
  N16: U1.TXD, ESP32_-_Front1.GPIO3_/_RX
  N17: M1.pin_1, L298N1.OUT1
  N18: M1.pin_2, L298N1.OUT2
  N19: M2.pin_1, L298N1.OUT3
  N20: M2.pin_2, L298N1.OUT4
  N21: L298N1.12V, U3.+
  VCC: HC-SR04_Sensor_2.VCC, ESP32_-_Front1.5V, U5.+
  N22: ESP32_-_Front1.GPIO15, Componente4.S
  N23: ESP32_-_Front1.GND#16, Componente4.GND
  N24: U2.+, U3.-
  N25: U4.+, U5.-

custom parts:
  L298N DC motor driver: 2x DC motor driver with 78M05 positive voltage regulator (7..35 V) L298N: max 46 V, 2 A Set 5 V Enable jumper to enable 5 V regultor (needed for the L298N) and +5 V output at screw terminal or supply external +5 V at screw terminal Set ENA and/or ENB to +5 V to enable motor permanently or supply ENA and/or ENB with PWM signal IN1 and IN2 set rotation directory for motor A (OUT1/OUT2) IN2 and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
  ESP32 - CAM: The ESP32-CAM has a very competitive small-size camera module that can operate independently as a minimum system with a footprint of only 27*40.5*4.5mm and a deep sleep current of up to 6mA.
  Keyes Photo Resistor Sensor: Keyes Photo Resistor Sensor Module for Arduino.
  KY-033 Tracing Black White Line Hunting Sensor Module For Arduino: Tracing Black White Line Hunting Sensor Module For Arduino Description: This is KY-033 tracking sensor. The KY-033 measures the intensity of infrared radiation and delivers it as an analog output voltage. Features: Operating voltage: 2.5 - 12V(cannot over12V) working current: 18mA-20mA at 5V Enhanced accuracy Documents: http://www.vishay.com/docs/83760/tcrt5000.pdf
